# Fritzing sketch Version1_onlyMotor (saved by Fritzing 0.9.2b)
breadboards: 2

parts:
  Teensy_3_1 = Teensy 3.1
  Q1 = Basic FET P-Channel [package="TO220 [THT]"]
  M1 = DC Motor

nets:
  N1: Teensy_3_1.GND, M1.pin_2
  N2: Teensy_3_1.D12, Q1.gate
  N3: Teensy_3_1.Vin, Q1.source
  N4: Q1.drain, M1.pin_1
